// Logisim project Lab2-prob1.circ as structural Verilog: 1 circuit, main circuit main
module main (
  input  a,
  input  a_2,
  input  b,
  input  b_2,
  input  c,
  input  c_2,
  input  a_3,
  input  a_4,
  input  b_3,
  input  b_4,
  input  c_3,
  input  c_4,
  output F,
  output out_14,
  output G,
  output G_2
);

  wire and_1_out, and_2_out, and_3_out, and_4_out, and_5_out, and_6_out, and_7_out, and_8_out, and_9_out,
       and_10_out, and_11_out, and_12_out, and_13_out, not_1_out, not_2_out, not_3_out, not_4_out, or_1_out,
       or_3_out, or_4_out, or_5_out, or_8_out;

  not not_1 (not_1_out, a_3);
  not not_2 (not_2_out, b_3);
  and and_1 (and_1_out, a_3, b_3);
  and and_2 (and_2_out, and_1_out, c_3);
  and and_3 (and_3_out, a, b_2);
  and and_4 (and_4_out, a_3, not_2_out);
  and and_5 (and_5_out, and_4_out, c_3);
  or or_1 (or_1_out, and_2_out, and_5_out);
  and and_6 (and_6_out, and_3_out, c);
  and and_7 (and_7_out, not_1_out, not_2_out);
  or or_2 (G_2, or_1_out, and_8_out);
  or or_3 (or_3_out, and_6_out, and_3_out);
  and and_8 (and_8_out, and_7_out, c_3);
  or or_4 (or_4_out, or_3_out, a);
  or or_5 (or_5_out, or_4_out, b_2);
  or or_6 (F, or_5_out, c);
  not not_3 (not_3_out, a_4);
  not not_4 (not_4_out, b_4);
  and and_9 (and_9_out, a_4, b_4, c_4);
  and and_10 (and_10_out, a_2, b, c_2);
  and and_11 (and_11_out, a_2, b);
  and and_12 (and_12_out, a_4, not_4_out, c_4);
  or or_7 (G, and_9_out, and_12_out, and_13_out);
  or or_8 (or_8_out, a_2, b, c_2);
  and and_13 (and_13_out, not_3_out, not_4_out, c_4);
  or or_9 (out_14, and_10_out, and_11_out, or_8_out);
endmodule
