// Logisim project Lab2-prob3.circ as structural Verilog
module main (
  input  Car1,
  input  Car5,
  input  Car2,
  input  Car3,
  input  Car6,
  input  in_6
);

  wire A_2_out, A_out, and_1_out, and_2_out, and_3_out, and_4_out, and_5_out, and_6_out, and_7_out, B_2_out,
       B_out, C_2_out, C_out, D_2_out, D_out, E_2_out, E_out, F_2_out, F_out, G_2_out, G_out, not_1_out,
       not_2_out, not_3_out, not_4_out, not_5_out, not_6_out, not_7_out, not_8_out, not_9_out, not_10_out,
       not_11_out, not_12_out, or_1_out, or_2_out, or_3_out;

  or or_1 (or_1_out, Car5, Car1, Car3);
  or or_2 (or_2_out, Car2, Car3, Car6);
  or or_3 (or_3_out, Car5, Car6, in_6);
  not not_1 (not_1_out, or_1_out);
  not not_2 (not_2_out, or_2_out);
  not not_3 (not_3_out, or_2_out);
  not not_4 (not_4_out, or_1_out);
  not not_5 (not_5_out, or_1_out);
  not not_6 (not_6_out, or_2_out);
  not not_7 (not_7_out, or_1_out);
  not not_8 (not_8_out, or_3_out);
  not not_9 (not_9_out, or_3_out);
  not not_10 (not_10_out, or_3_out);
  not not_11 (not_11_out, or_3_out);
  not not_12 (not_12_out, or_2_out);
  and and_1 (and_1_out, not_1_out, not_2_out, not_8_out);
  and and_2 (and_2_out, or_1_out, not_3_out, not_3_out, not_9_out);
  and and_3 (and_3_out, not_4_out, or_2_out, not_10_out);
  and and_4 (and_4_out, or_1_out, or_2_out, not_11_out);
  and and_5 (and_5_out, not_5_out, not_12_out, or_3_out);
  and and_6 (and_6_out, or_1_out, not_6_out, or_3_out, or_3_out);
  and and_7 (and_7_out, not_7_out, or_2_out, or_3_out);
  or A (A_out, and_1_out, and_3_out, and_4_out);
  or B (B_out, and_1_out, and_2_out, and_3_out, and_4_out, and_5_out);
  or C (C_out, and_1_out, and_2_out, and_4_out, and_5_out);
  or D (D_out, and_1_out, and_3_out, and_4_out);
  or E (E_out, and_1_out, and_3_out);
  or F (F_out, and_1_out, and_5_out);
  or G (G_out, and_3_out, and_4_out, and_5_out);
  _7_Segment_Display u_7_segment_display_1 (
    .g(G_2_out), .f(F_2_out), .a(A_2_out), .b(B_2_out), .e(E_2_out), .d(D_2_out), .c(C_2_out));  // open: dp
  or A_2 (A_2_out, and_6_out, and_7_out, A_out);
  buf B_2 (B_2_out, B_out);  // OR_Gate
  or C_2 (C_2_out, and_6_out, and_7_out, C_out);
  or D_2 (D_2_out, and_6_out, and_7_out, D_out);
  or E_2 (E_2_out, E_out, and_7_out);
  or F_2 (F_2_out, and_6_out, and_7_out, F_out);
  or G_2 (G_2_out, and_6_out, and_7_out, G_out);

  // Notes on the sheet:
  //   O1
  //   O2
  //   O3
  //   Car4
  //   Decoder
  //   Motor Car
  //   Car1
  //   Car2
  //   Car3
  //   Car4
  //   Car5
  //   Car6
endmodule
